// Digital circuit 1-bit-Register.dig as structural Verilog
module _1_bit_Register (
  input  data,
  input  enable,
  input  clock,
  output Q
);

  wire and_1_out, and_2_out, not_1_out, not_2_out, or_1_out;

  not not_1 (not_1_out, enable);
  and and_1 (and_1_out, Q, not_1_out);
  and and_2 (and_2_out, data, enable);
  or or_1 (or_1_out, and_1_out, and_2_out);
  not not_2 (not_2_out, clock);
  D_Latch d_latch_1 ();
  D_Latch d_latch_2 ();
endmodule
