// Digital circuit 1-bit-adder.dig as structural Verilog
module _1_bit_adder (
  input  n1i,
  input  n2i,
  input  carry_in,
  output carry_out,
  output res
);

  wire nand_1_out, nand_2_out, nand_3_out, nand_4_out, nand_5_out, nand_6_out, nand_7_out, nand_8_out,
       nand_9_out, nand_10_out, nand_11_out, nand_12_out, nand_13_out, nand_14_out, nand_15_out, nand_16_out,
       nand_17_out, nand_18_out;

  nand nand_1 (nand_1_out, n1i, n2i);
  nand nand_2 (nand_2_out, n1i, nand_1_out);
  nand nand_3 (nand_3_out, nand_1_out, n2i);
  nand nand_4 (nand_4_out, n1i, n2i);
  nand nand_5 (nand_5_out, n1i, carry_in);
  nand nand_6 (nand_6_out, n2i, carry_in);
  nand nand_7 (nand_7_out, nand_2_out, nand_3_out);
  nand nand_8 (nand_8_out, nand_4_out, nand_4_out);
  nand nand_9 (nand_9_out, nand_5_out, nand_5_out);
  nand nand_10 (nand_10_out, nand_6_out, nand_6_out);
  nand nand_11 (nand_11_out, nand_9_out, nand_9_out);
  nand nand_12 (nand_12_out, nand_10_out, nand_10_out);
  nand nand_13 (nand_13_out, carry_in, nand_7_out);
  nand nand_14 (nand_14_out, nand_11_out, nand_12_out);
  nand nand_15 (nand_15_out, carry_in, nand_13_out);
  nand nand_16 (nand_16_out, nand_13_out, nand_7_out);
  nand nand_17 (nand_17_out, nand_8_out, nand_8_out);
  nand nand_18 (nand_18_out, nand_14_out, nand_14_out);
  nand nand_19 (res, nand_15_out, nand_16_out);
  nand nand_20 (carry_out, nand_17_out, nand_18_out);

  // Notes on the sheet:
  //   n_1 bit
  //   n_2 bit
  //   carry_in bit
  //   1 BIT ADDER
  //   n1i+n2i
  //   n1i+carry_in
  //   n2i+carry_in
  //   res bit
  //   carry_out bit
endmodule
