// Digital circuit 1-bit-subtractor.dig as structural Verilog
module _1_bit_subtractor (
  input  n1,
  input  n2,
  input  borrow_in,
  output borrow_out,
  output res
);

  wire and_1_out, and_2_out, and_3_out, not_1_out, not_2_out, or_1_out, xor_1_out;

  xor xor_1 (xor_1_out, n1, n2);
  not not_1 (not_1_out, n1);
  and and_1 (and_1_out, not_1_out, n2);
  and and_2 (and_2_out, not_2_out, borrow_in);
  not not_2 (not_2_out, n1);
  xor xor_2 (res, xor_1_out, borrow_in);
  and and_3 (and_3_out, n2, borrow_in);
  or or_1 (or_1_out, and_1_out, and_2_out);
  or or_2 (borrow_out, or_1_out, and_3_out);

  // Notes on the sheet:
  //   1 BIT SUBTRACTOR
endmodule
