// Digital circuit 2x1-Mux.dig as structural Verilog
module _2x1_Mux (
  input  data_1,
  input  data_2,
  input  select,
  output val
);

  wire and_1_out, and_2_out, not_1_out;

  not not_1 (not_1_out, select);
  and and_1 (and_1_out, data_1, not_1_out);
  and and_2 (and_2_out, data_2, select);
  or or_1 (val, and_1_out, and_2_out);

  // Notes on the sheet:
  //   val: pin 6
  //   data_1: pin 1
  //   data_2: pin 2
  //   select: pin 3
endmodule
