// Digital circuit 3-bit-Register.dig as structural Verilog
module _3_bit_Register (
  input  n_1,
  input  n_2,
  input  n_3,
  input  enable,
  input  clock,
  output val_1,
  output val_2,
  output val_3
);

  _1_bit_Register _1_bit_register_1 (.data(n_1), .enable(enable), .clock(clock), .Q(val_1));
  _1_bit_Register _1_bit_register_2 (.data(n_2), .enable(enable), .clock(clock), .Q(val_2));
  _1_bit_Register _1_bit_register_3 (.data(n_3), .enable(enable), .clock(clock), .Q(val_3));
endmodule
