// Digital circuit 3-bit-adder.dig as structural Verilog
module _3_bit_adder (
  input  n2_1,
  input  n2_2,
  input  n2_3,
  input  n1_1,
  input  n1_2,
  input  n1_3,
  input  carry_in,
  output C_out,
  output val_1,
  output val_2,
  output val_3
);

  wire nand_1_out, nand_2_out, nand_3_out, nand_4_out, nand_5_out, nand_6_out, nand_7_out, nand_8_out,
       nand_9_out, nand_10_out, nand_11_out, nand_12_out, nand_13_out, nand_14_out, nand_15_out, nand_16_out,
       nand_17_out, nand_18_out, nand_19_out, nand_20_out, nand_21_out, nand_22_out, nand_23_out,
       nand_24_out, nand_25_out, nand_26_out, nand_27_out, nand_28_out, nand_29_out, nand_30_out,
       nand_31_out, nand_32_out, nand_33_out, nand_34_out, nand_35_out, nand_36_out, nand_37_out,
       nand_38_out, nand_39_out, nand_40_out, nand_41_out, nand_42_out, nand_43_out, nand_44_out,
       nand_45_out, nand_46_out, nand_47_out, nand_48_out, nand_49_out, nand_50_out, nand_51_out,
       nand_52_out, nand_53_out, nand_54_out, nand_59_out, nand_60_out;

  nand nand_1 (nand_1_out, n1_3, n2_3);
  nand nand_2 (nand_2_out, n1_1, n2_1);
  nand nand_3 (nand_3_out, n1_2, n2_2);
  nand nand_4 (nand_4_out, n1_3, nand_1_out);
  nand nand_5 (nand_5_out, nand_1_out, n2_3);
  nand nand_6 (nand_6_out, n1_1, nand_2_out);
  nand nand_7 (nand_7_out, nand_2_out, n2_1);
  nand nand_8 (nand_8_out, n1_2, nand_3_out);
  nand nand_9 (nand_9_out, nand_3_out, n2_2);
  nand nand_10 (nand_10_out, n1_2, n2_2);
  nand nand_11 (nand_11_out, n1_2, nand_60_out);
  nand nand_12 (nand_12_out, n2_2, nand_60_out);
  nand nand_13 (nand_13_out, n1_3, n2_3);
  nand nand_14 (nand_14_out, n1_3, carry_in);
  nand nand_15 (nand_15_out, n2_3, carry_in);
  nand nand_16 (nand_16_out, n1_1, n2_1);
  nand nand_17 (nand_17_out, n1_1, nand_59_out);
  nand nand_18 (nand_18_out, n2_1, nand_59_out);
  nand nand_19 (nand_19_out, nand_4_out, nand_5_out);
  nand nand_20 (nand_20_out, nand_6_out, nand_7_out);
  nand nand_21 (nand_21_out, nand_8_out, nand_9_out);
  nand nand_22 (nand_22_out, nand_10_out, nand_10_out);
  nand nand_23 (nand_23_out, nand_11_out, nand_11_out);
  nand nand_24 (nand_24_out, nand_12_out, nand_12_out);
  nand nand_25 (nand_25_out, nand_13_out, nand_13_out);
  nand nand_26 (nand_26_out, nand_14_out, nand_14_out);
  nand nand_27 (nand_27_out, nand_15_out, nand_15_out);
  nand nand_28 (nand_28_out, nand_16_out, nand_16_out);
  nand nand_29 (nand_29_out, nand_17_out, nand_17_out);
  nand nand_30 (nand_30_out, nand_18_out, nand_18_out);
  nand nand_31 (nand_31_out, nand_23_out, nand_23_out);
  nand nand_32 (nand_32_out, nand_24_out, nand_24_out);
  nand nand_33 (nand_33_out, nand_26_out, nand_26_out);
  nand nand_34 (nand_34_out, nand_27_out, nand_27_out);
  nand nand_35 (nand_35_out, nand_29_out, nand_29_out);
  nand nand_36 (nand_36_out, nand_30_out, nand_30_out);
  nand nand_37 (nand_37_out, nand_60_out, nand_21_out);
  nand nand_38 (nand_38_out, carry_in, nand_19_out);
  nand nand_39 (nand_39_out, nand_59_out, nand_20_out);
  nand nand_40 (nand_40_out, nand_31_out, nand_32_out);
  nand nand_41 (nand_41_out, nand_33_out, nand_34_out);
  nand nand_42 (nand_42_out, nand_35_out, nand_36_out);
  nand nand_43 (nand_43_out, nand_60_out, nand_37_out);
  nand nand_44 (nand_44_out, nand_37_out, nand_21_out);
  nand nand_45 (nand_45_out, carry_in, nand_38_out);
  nand nand_46 (nand_46_out, nand_38_out, nand_19_out);
  nand nand_47 (nand_47_out, nand_59_out, nand_39_out);
  nand nand_48 (nand_48_out, nand_39_out, nand_20_out);
  nand nand_49 (nand_49_out, nand_22_out, nand_22_out);
  nand nand_50 (nand_50_out, nand_40_out, nand_40_out);
  nand nand_51 (nand_51_out, nand_25_out, nand_25_out);
  nand nand_52 (nand_52_out, nand_41_out, nand_41_out);
  nand nand_53 (nand_53_out, nand_28_out, nand_28_out);
  nand nand_54 (nand_54_out, nand_42_out, nand_42_out);
  nand nand_55 (val_2, nand_43_out, nand_44_out);
  nand nand_56 (val_3, nand_45_out, nand_46_out);
  nand nand_57 (val_1, nand_47_out, nand_48_out);
  nand nand_58 (C_out, nand_53_out, nand_54_out);
  nand nand_59 (nand_59_out, nand_49_out, nand_50_out);
  nand nand_60 (nand_60_out, nand_51_out, nand_52_out);

  // Notes on the sheet:
  //   n_1 bit
  //   n_2 bit
  //   carry_in bit
  //   n1i+n2i
  //   n1i+carry_in
  //   n2i+carry_in
  //   3 BIT ADDER
  //   res bit
  //   carry_out bit
endmodule
