// Digital circuit 4-bit-Adder.dig as structural Verilog
module _4_bit_Adder (
  input  n1_1,
  input  n1_2,
  input  n1_3,
  input  n1_4,
  input  n2_1,
  input  n2_2,
  input  n2_3,
  input  n2_4,
  output res_1,
  output res_2,
  output res_3,
  output res_4,
  output C_out
);

  wire _1_bit_adder_2_c_out, _1_bit_adder_3_c_out, _1_bit_adder_4_c_out, xor_1_out;

  xor xor_1 (xor_1_out, n2_4, n2_4);
  _1_bit_Adder _1_bit_adder_1 (.res(res_1), .C_out(C_out), .n_1(n1_1), .n_2(n2_1), .C_in(_1_bit_adder_2_c_out));
  _1_bit_Adder _1_bit_adder_2 (
    .res(res_2), .C_out(_1_bit_adder_2_c_out), .n_1(n1_2), .n_2(n2_2), .C_in(_1_bit_adder_3_c_out));
  _1_bit_Adder _1_bit_adder_3 (
    .res(res_3), .C_out(_1_bit_adder_3_c_out), .n_1(n1_3), .n_2(n2_3), .C_in(_1_bit_adder_4_c_out));
  _1_bit_Adder _1_bit_adder_4 (.res(res_4), .C_out(_1_bit_adder_4_c_out), .n_1(n1_4), .n_2(n2_4), .C_in(xor_1_out));
  LED led_1 (.in(xor_1_out));

  // Notes on the sheet:
  //   n1_1: pin 1
  //   n1_2: pin 2
  //   n1_3: pin 3
  //   n1_4: pin 4
  //   n2_1: pin 5
  //   n2_2: pin 6
  //   res_1: pin 16
  //   res_2: pin 15
  //   res_3: pin 14
  //   res_4: pin 13
  //   n2_3: pin 7
  //   n2_4: pin 8
  //   C_out: pin 9
endmodule
