// Digital circuit 4-bit-Inverter.dig as structural Verilog
module _4_bit_Inverter (
  input  n_1,
  input  n_2,
  input  n_3,
  input  n_4,
  output val2,
  output val1,
  output val3,
  output val4
);

  nand nand_1 (val1, n_1, n_1);
  nand nand_2 (val2, n_2, n_2);
  nand nand_3 (val3, n_3, n_3);
  nand nand_4 (val4, n_4, n_4);

  // Notes on the sheet:
  //   val2: pin 10
  //   val1: pin 11
  //   val3: pin 9
  //   val4: pin 8
  //   INV CI
endmodule
