// Digital circuit 4-bit-Register.dig as structural Verilog
module _4_bit_Register (
  input  enable,
  input  clock,
  input  n_1,
  input  n_2,
  input  n_3,
  input  n_4,
  output val_1,
  output val_2,
  output val_3,
  output val_4
);

  _1_bit_Register _1_bit_register_1 (.data(n_1), .enable(enable), .clock(clock), .Q(val_1));
  _1_bit_Register _1_bit_register_2 (.data(n_2), .enable(enable), .clock(clock), .Q(val_2));
  _1_bit_Register _1_bit_register_3 (.data(n_3), .enable(enable), .clock(clock), .Q(val_3));
  _1_bit_Register _1_bit_register_4 (.data(n_4), .enable(enable), .clock(clock), .Q(val_4));
  LED led_1 (.in(val_1));
  LED led_2 (.in(val_2));
  LED led_3 (.in(val_3));
  LED led_4 (.in(val_4));

  // Notes on the sheet:
  //   enable: pin 5
  //   clock: pin 6
  //   n_1: pin 1
  //   n_2: pin 2
  //   n_3: pin 3
  //   n_4: pin 4
  //   val_1: pin 12
  //   val_2: pin 11
  //   val_3: pin 10
  //   val_4: pin 9
endmodule
