// Digital circuit 4x1-Mux.dig as structural Verilog
module _4x1_Mux (
  input  select_1,
  input  select_2,
  input  data_1,
  input  data_2,
  input  data_3,
  input  data_4,
  output val
);

  wire _2x1_mux_1_val, _2x1_mux_2_val;

  _2x1_Mux _2x1_mux_1 (.val(_2x1_mux_1_val), .data_1(data_1), .data_2(data_2), .select(select_2));
  _2x1_Mux _2x1_mux_2 (.val(_2x1_mux_2_val), .data_1(data_4), .data_2(data_3), .select(select_2));
  _2x1_Mux _2x1_mux_3 (.val(val), .data_1(_2x1_mux_1_val), .data_2(_2x1_mux_2_val), .select(select_1));

  // Notes on the sheet:
  //   val: pin 12
  //   select_1: pin 5
  //   select_2: pin 6
  //   data_1: pin 1
  //   data_2: pin 2
  //   data_3: pin 4
  //   data_4: pin 3
endmodule
