// Digital circuit 7-segment.dig as structural Verilog
module _7_segment (
  input  n_1,
  input  n_2,
  input  n_3,
  output top_1,
  output top_2,
  output top_3,
  output top_4,
  output bot_1,
  output bot_2,
  output bot_3,
  output bot_4
);

  wire nand_1_out, nand_2_out, nand_3_out, nand_4_out, nand_5_out, nand_6_out, nand_7_out, nand_8_out,
       nand_9_out, nand_10_out, nand_11_out, nand_12_out, nand_13_out, nand_14_out, nand_15_out, nand_16_out,
       nand_17_out, nand_18_out, nand_19_out, nand_20_out, nand_21_out, nand_22_out, nand_23_out,
       nand_24_out, nand_25_out, nand_26_out, nand_27_out, nand_28_out, nand_29_out, nand_30_out,
       nand_31_out, nand_32_out, nand_33_out, nand_34_out, nand_35_out, nand_36_out, nand_37_out,
       nand_38_out, nand_39_out, nand_40_out, nand_41_out, nand_42_out, nand_43_out, nand_44_out,
       nand_45_out, nand_46_out, nand_47_out, nand_48_out, nand_49_out, nand_50_out, nand_51_out,
       nand_52_out, nand_53_out, nand_54_out, nand_55_out, nand_56_out, nand_57_out, nand_58_out,
       nand_59_out, nand_60_out, nand_61_out, nand_62_out, nand_66_out, nand_67_out, nand_69_out,
       nand_70_out, nand_71_out, nand_72_out, nand_73_out, nand_75_out, nand_76_out, nand_77_out,
       nand_78_out, nand_79_out, nand_80_out, nand_81_out, nand_82_out, nand_83_out, nand_84_out,
       nand_85_out, nand_86_out, nand_87_out, nand_88_out;

  nand nand_1 (nand_1_out, n_2, n_2);
  nand nand_2 (nand_2_out, n_1, n_1);
  nand nand_3 (nand_3_out, n_3, n_3);
  nand nand_4 (nand_4_out, n_2, n_2);
  nand nand_5 (nand_5_out, n_1, n_1);
  nand nand_6 (nand_6_out, n_3, n_3);
  nand nand_7 (nand_7_out, n_3, n_3);
  nand nand_8 (nand_8_out, n_2, n_2);
  nand nand_9 (nand_9_out, n_3, n_3);
  nand nand_10 (nand_10_out, n_3, n_3);
  nand nand_11 (nand_11_out, n_2, nand_7_out);
  nand nand_12 (nand_12_out, nand_8_out, nand_9_out);
  nand nand_13 (nand_13_out, n_1, nand_1_out);
  nand nand_14 (nand_14_out, nand_2_out, n_2);
  nand nand_15 (nand_15_out, n_2, nand_10_out);
  nand nand_16 (nand_16_out, n_2, nand_3_out);
  nand nand_17 (nand_17_out, n_1, nand_4_out);
  nand nand_18 (nand_18_out, nand_5_out, nand_6_out);
  nand nand_19 (nand_19_out, nand_18_out, nand_18_out);
  nand nand_20 (nand_20_out, nand_11_out, nand_11_out);
  nand nand_21 (nand_21_out, nand_12_out, nand_12_out);
  nand nand_22 (nand_22_out, nand_13_out, nand_13_out);
  nand nand_23 (nand_23_out, nand_14_out, nand_14_out);
  nand nand_24 (nand_24_out, nand_15_out, nand_15_out);
  nand nand_25 (nand_25_out, nand_16_out, nand_16_out);
  nand nand_26 (nand_26_out, nand_17_out, nand_17_out);
  nand nand_27 (nand_27_out, n_1, n_1);
  nand nand_28 (nand_28_out, n_3, n_3);
  nand nand_29 (nand_29_out, n_1, n_1);
  nand nand_30 (nand_30_out, n_3, n_3);
  nand nand_31 (nand_31_out, n_2, n_2);
  nand nand_32 (nand_32_out, n_1, n_1);
  nand nand_33 (nand_33_out, n_3, n_3);
  nand nand_34 (nand_34_out, n_2, n_2);
  nand nand_35 (nand_35_out, n_1, n_1);
  nand nand_36 (nand_36_out, n_3, n_3);
  nand nand_37 (nand_37_out, nand_21_out, nand_21_out);
  nand nand_38 (nand_38_out, nand_22_out, nand_22_out);
  nand nand_39 (nand_39_out, nand_23_out, nand_23_out);
  nand nand_40 (nand_40_out, nand_24_out, nand_24_out);
  nand nand_41 (nand_41_out, nand_66_out, nand_66_out);
  nand nand_42 (nand_42_out, nand_25_out, nand_25_out);
  nand nand_43 (nand_43_out, nand_67_out, nand_67_out);
  nand nand_44 (nand_44_out, nand_26_out, nand_26_out);
  nand nand_45 (nand_45_out, nand_27_out, nand_28_out);
  nand nand_46 (nand_46_out, nand_29_out, n_2);
  nand nand_47 (nand_47_out, n_2, nand_30_out);
  nand nand_48 (nand_48_out, n_1, nand_31_out);
  nand nand_49 (nand_49_out, nand_32_out, nand_33_out);
  nand nand_50 (nand_50_out, nand_49_out, nand_49_out);
  nand nand_51 (nand_51_out, nand_34_out, nand_34_out);
  nand nand_52 (nand_52_out, nand_35_out, nand_35_out);
  nand nand_53 (nand_53_out, nand_36_out, nand_36_out);
  nand nand_54 (nand_54_out, n_3, n_3);
  nand nand_55 (nand_55_out, n_1, n_1);
  nand nand_56 (nand_56_out, n_3, n_1);
  nand nand_57 (nand_57_out, nand_19_out, nand_19_out);
  nand nand_58 (nand_58_out, nand_20_out, nand_20_out);
  nand nand_59 (nand_59_out, nand_45_out, nand_45_out);
  nand nand_60 (nand_60_out, nand_46_out, nand_46_out);
  nand nand_61 (nand_61_out, nand_47_out, nand_47_out);
  nand nand_62 (nand_62_out, nand_48_out, nand_48_out);
  nand nand_63 (top_3, nand_50_out, nand_51_out);
  nand nand_64 (bot_1, nand_57_out, nand_58_out);
  nand nand_65 (bot_2, nand_37_out, nand_38_out);
  nand nand_66 (nand_66_out, nand_39_out, nand_40_out);
  nand nand_67 (nand_67_out, nand_41_out, nand_42_out);
  nand nand_68 (bot_3, nand_43_out, nand_44_out);
  nand nand_69 (nand_69_out, nand_52_out, nand_53_out);
  nand nand_70 (nand_70_out, nand_69_out, nand_69_out);
  nand nand_71 (nand_71_out, n_2, n_2);
  nand nand_72 (nand_72_out, nand_54_out, nand_55_out);
  nand nand_73 (nand_73_out, nand_56_out, nand_56_out);
  nand nand_74 (top_2, nand_70_out, nand_71_out);
  nand nand_75 (nand_75_out, nand_73_out, nand_73_out);
  nand nand_76 (nand_76_out, n_2, n_2);
  nand nand_77 (nand_77_out, nand_72_out, nand_72_out);
  nand nand_78 (nand_78_out, nand_75_out, nand_76_out);
  nand nand_79 (nand_79_out, nand_59_out, nand_59_out);
  nand nand_80 (nand_80_out, nand_60_out, nand_60_out);
  nand nand_81 (nand_81_out, nand_87_out, nand_87_out);
  nand nand_82 (nand_82_out, nand_61_out, nand_61_out);
  nand nand_83 (nand_83_out, nand_88_out, nand_88_out);
  nand nand_84 (nand_84_out, nand_62_out, nand_62_out);
  nand nand_85 (nand_85_out, nand_77_out, nand_77_out);
  nand nand_86 (nand_86_out, nand_78_out, nand_78_out);
  nand nand_87 (nand_87_out, nand_79_out, nand_80_out);
  nand nand_88 (nand_88_out, nand_81_out, nand_82_out);
  nand nand_89 (top_4, nand_83_out, nand_84_out);
  nand nand_90 (top_1, nand_85_out, nand_86_out);
  Switch switch_1 (.A(bot_3), .B(bot_4));

  // Notes on the sheet:
  //   top_1: pin 16
  //   top_2: pin 15
  //   top_3: pin 14
  //   top_4: pin 13
  //   bot_1: pin 12
  //   bot_2: pin 11
  //   bot_3: pin 10
  //   bot_4: pin 9
  //   val_1
  //   val_3
  //   val_2
  //   7 SEGMENT CI DISPLAY
  //   I_6
  //   I_7
  //   I_3
  //   I_5
  //   I_2
  //   I_4
  //   I_1
endmodule
