// Digital circuit 8x1-Mux.dig as structural Verilog
module _8x1_Mux (
  input  select_1,
  input  select_2,
  input  select_3,
  input  data_1,
  input  data_3,
  input  data_5,
  input  data_7,
  input  data_2,
  input  data_4,
  input  data_6,
  input  data_8,
  output val
);

  wire _4x1_mux_1_val, _4x1_mux_2_val;

  _4x1_Mux _4x1_mux_1 (
    .val(_4x1_mux_1_val), .select_1(select_1), .select_2(select_2), .data_1(data_1), .data_2(data_3),
    .data_3(data_7), .data_4(data_5));
  _4x1_Mux _4x1_mux_2 (
    .val(_4x1_mux_2_val), .select_1(select_1), .select_2(select_2), .data_1(data_2), .data_2(data_4),
    .data_3(data_8), .data_4(data_6));
  _2x1_Mux _2x1_mux_1 (.val(val), .data_1(_4x1_mux_1_val), .data_2(_4x1_mux_2_val), .select(select_3));

  // Notes on the sheet:
  //   select_1: pin 11
  //   select_2: pin 10
  //   select_3: pin 9
  //   data_1: pin 1
  //   data_3: pin 3
  //   data_5: pin 5
  //   data_7: pin 7
  //   data_2: pin 2
  //   data_4: pin 4
  //   data_6: pin 6
  //   data_8: pin 8
  //   val: pin 16
endmodule
