// Digital circuit Counter.dig as structural Verilog
module Counter (
  input  clk,
  input  enable,
  input  _1
);

  wire _3_bit_adder_1_c_out, _3_bit_adder_1_val_1, _3_bit_adder_1_val_2, _3_bit_adder_1_val_3,
       _7_segment_1_bot_1, _7_segment_1_bot_2, _7_segment_1_bot_3, _7_segment_1_bot_4, _7_segment_1_top_1,
       _7_segment_1_top_2, _7_segment_1_top_3, _7_segment_1_top_4, not_1_out, not_2_out, Register_A_val_1,
       Register_A_val_2, Register_A_val_3, Register_B_val_1, Register_B_val_2, Register_B_val_3;

  not not_1 (not_1_out, _1);
  not not_2 (not_2_out, _1);
  _3_bit_Register Register_A (
    .n_1(_3_bit_adder_1_val_1), .n_2(_3_bit_adder_1_val_2), .n_3(_3_bit_adder_1_val_3), .enable(enable),
    .clock(clk), .val_1(Register_A_val_1), .val_2(Register_A_val_2), .val_3(Register_A_val_3));
  _3_bit_Register Register_B (
    .n_1(not_1_out), .n_2(not_2_out), .n_3(_1), .enable(enable), .clock(clk), .val_1(Register_B_val_1),
    .val_2(Register_B_val_2), .val_3(Register_B_val_3));
  _7_Segment _7_segment_1 (
    .n_1(Register_A_val_1), .n_2(Register_A_val_2), .n_3(Register_A_val_3), .top_1(_7_segment_1_top_1),
    .top_2(_7_segment_1_top_2), .top_3(_7_segment_1_top_3), .top_4(_7_segment_1_top_4),
    .bot_1(_7_segment_1_bot_1), .bot_2(_7_segment_1_bot_2), .bot_3(_7_segment_1_bot_3),
    .bot_4(_7_segment_1_bot_4));
  LED B_1 (.in(Register_B_val_1));
  LED B_2 (.in(Register_B_val_2));
  LED B_3 (.in(Register_B_val_3));
  _3_bit_Adder _3_bit_adder_1 (
    .n2_1(Register_A_val_1), .n2_2(Register_A_val_1), .n2_3(Register_A_val_1), .n1_1(Register_B_val_1),
    .n1_2(Register_B_val_2), .n1_3(Register_B_val_3), .carry_in(_3_bit_adder_1_c_out),
    .C_out(_3_bit_adder_1_c_out), .val_1(_3_bit_adder_1_val_1), .val_2(_3_bit_adder_1_val_2),
    .val_3(_3_bit_adder_1_val_3));
  Seven_Seg seven_seg_1 (
    .a(_7_segment_1_top_1), .b(_7_segment_1_top_2), .c(_7_segment_1_top_3), .d(_7_segment_1_top_4),
    .e(_7_segment_1_bot_1), .f(_7_segment_1_bot_2), .g(_7_segment_1_bot_3), .dp(_7_segment_1_bot_4));

  // Notes on the sheet:
  //   enable: default 1
  //   _1: default 1
endmodule
