// Digital circuit D-FlipFlop-Enabable.dig as structural Verilog
module D_FlipFlop_Enabable (
  input  data,
  input  enable,
  input  clock,
  output Q
);

  wire and_1_out, not_1_out;

  and and_1 (and_1_out, clock, enable);
  not not_1 (not_1_out, and_1_out);
  D_Latch d_latch_1 ();
  D_Latch d_latch_2 ();
endmodule
