// Digital circuit D-Latch.dig as structural Verilog
module D_Latch (
  input  data,
  input  enable,
  output Q,
  output nQ
);

  wire and_1_out, and_2_out, not_1_out, not_2_out, not_3_out;

  not not_1 (not_1_out, data);
  and and_1 (and_1_out, data, enable);
  and and_2 (and_2_out, enable, not_1_out);
  not not_2 (not_2_out, and_1_out);
  not not_3 (not_3_out, and_2_out);
  nand nand_1 (Q, not_2_out, nQ);
  nand nand_2 (nQ, Q, not_3_out);
endmodule
