// Digital circuit FSD - 00,21.dig as structural Verilog
module FSD___00_21 (
  input  addr1,
  input  addr2,
  input  addr3,
  input  addr1_3,
  input  addr2_3,
  input  addr3_3,
  input  n21,
  input  n22,
  input  n23,
  input  n11,
  input  n12,
  input  n13,
  input  addr1_5,
  input  addr2_5,
  input  addr3_5,
  input  n21_2,
  input  n22_2,
  input  n23_2,
  input  n1i,
  input  n2i,
  input  carry_in,
  output val2,
  output val1,
  output addr1_2,
  output val3,
  output addr3_2,
  output addr2_2,
  output val2_2,
  output val1_2,
  output addr1_4,
  output val3_2,
  output addr3_4,
  output addr2_4,
  output val2_3,
  output val1_3,
  output addr1_6,
  output val3_3,
  output addr3_6,
  output addr2_6,
  output carry_out,
  output res
);

  wire nand_1_out, nand_2_out, nand_3_out, nand_4_out, nand_5_out, nand_6_out, nand_7_out, nand_8_out,
       nand_9_out, nand_10_out, nand_11_out, nand_12_out, nand_13_out, nand_14_out, nand_15_out, nand_16_out,
       nand_17_out, nand_18_out, nand_24_out, nand_25_out, nand_26_out, nand_27_out, nand_28_out,
       nand_29_out, nand_30_out;

  nand nand_1 (nand_1_out, n1i, n2i);
  nand nand_2 (nand_2_out, n1i, nand_1_out);
  nand nand_3 (nand_3_out, nand_1_out, n2i);
  nand nand_4 (nand_4_out, n1i, n2i);
  nand nand_5 (nand_5_out, n1i, carry_in);
  nand nand_6 (nand_6_out, n2i, carry_in);
  nand nand_7 (nand_7_out, nand_2_out, nand_3_out);
  nand nand_8 (nand_8_out, nand_4_out, nand_4_out);
  nand nand_9 (nand_9_out, nand_5_out, nand_5_out);
  nand nand_10 (nand_10_out, nand_6_out, nand_6_out);
  nand nand_11 (nand_11_out, nand_9_out, nand_9_out);
  nand nand_12 (nand_12_out, nand_10_out, nand_10_out);
  nand nand_13 (nand_13_out, carry_in, nand_7_out);
  nand nand_14 (nand_14_out, nand_11_out, nand_12_out);
  nand nand_15 (nand_15_out, carry_in, nand_13_out);
  nand nand_16 (nand_16_out, nand_13_out, nand_7_out);
  nand nand_17 (nand_17_out, nand_8_out, nand_8_out);
  nand nand_18 (nand_18_out, nand_14_out, nand_14_out);
  nand nand_19 (res, nand_15_out, nand_16_out);
  nand nand_20 (carry_out, nand_17_out, nand_18_out);
  nand nand_21 (val1_3, n21_2, n21_2);
  nand nand_22 (val2_3, n22_2, n22_2);
  nand nand_23 (val3_3, n23_2, n23_2);
  nand nand_24 (nand_24_out, n11, n11);
  nand nand_25 (nand_25_out, n21, n21);
  nand nand_26 (nand_26_out, n12, n12);
  nand nand_27 (nand_27_out, n22, n22);
  nand nand_28 (nand_28_out, n13, n13);
  nand nand_29 (nand_29_out, n23, n23);
  nand nand_30 (nand_30_out, addr1, addr1);
  nand nand_31 (val1_2, nand_24_out, nand_25_out);
  nand nand_32 (val2_2, nand_26_out, nand_27_out);
  nand nand_33 (val3_2, nand_28_out, nand_29_out);
  nand nand_34 (val1, nand_30_out, addr1);

  assign addr1_2 = addr1;
  assign addr1_4 = addr1_3;
  assign addr1_6 = addr1_5;
  assign addr2_2 = addr2;
  assign addr2_4 = addr2_3;
  assign addr2_6 = addr2_5;
  assign addr3_2 = addr3;
  assign addr3_4 = addr3_3;
  assign addr3_6 = addr3_5;
  assign val2 = val1;
  assign val3 = val1;

  // Notes on the sheet:
  //   n_1 bit
  //   n_2 bit
  //   carry_in bit
  //   n1i+n2i
  //   n1i+carry_in
  //   n2i+carry_in
  //   res bit
  //   carry_out bit
endmodule
