// Digital circuit Inv.dig as structural Verilog
module Inv (
  input  addr1,
  input  addr2,
  input  addr3,
  output val5,
  output val4,
  output addr1_2,
  output val6,
  output addr3_2,
  output addr2_2
);

  wire nand_1_out;

  nand nand_1 (nand_1_out, addr1, addr1);
  nand nand_2 (val4, nand_1_out, addr1);

  assign addr1_2 = addr1;
  assign addr2_2 = addr2;
  assign addr3_2 = addr3;
  assign val5 = val4;
  assign val6 = val4;

  // Notes on the sheet:
  //   INIT CI
endmodule
