// Digital circuit SR-Latch-Enabable.dig as structural Verilog
module SR_Latch_Enabable (
  input  set,
  input  clear,
  input  enable,
  output Q,
  output nQ
);

  wire and_1_out, and_2_out, not_1_out, not_2_out;

  and and_1 (and_1_out, set, enable);
  and and_2 (and_2_out, enable, clear);
  not not_1 (not_1_out, and_1_out);
  not not_2 (not_2_out, and_2_out);
  nand nand_1 (Q, not_1_out, nQ);
  nand nand_2 (nQ, Q, not_2_out);
endmodule
