// Digital circuit SR-Latch.dig as structural Verilog
module SR_Latch (
  input  set,
  input  clear,
  output Q,
  output nQ
);

  wire not_1_out, not_2_out;

  not not_1 (not_1_out, set);
  not not_2 (not_2_out, clear);
  nand nand_1 (Q, not_1_out, nQ);
  nand nand_2 (nQ, Q, not_2_out);
endmodule
