// Digital circuit Serial-Subtractor.dig as structural Verilog
module Serial_Subtractor (
  input  clock,
  input  n2_bit,
  input  n1_bit,
  input  enable,
  input  enable_borrow,
  input  enable_store,
  input  clock_4
);

  wire and_1_out, and_2_out, bit_1_p4, bit_2_p4, BORROW_in_out_p4, mem_1_p4, mem_2_p4, mem_3_p4,
       sub_borrow_out, sub_res, xor_1_out;

  // D_FlipFlop bit_1: pin names not known; wires that end beside it: n1_bit, enable, clock, bit_1_p4
  // D_FlipFlop bit_2: pin names not known; wires that end beside it: n2_bit, enable, clock, bit_2_p4
  and and_1 (and_1_out, sub_borrow_out, enable_borrow);
  LED led_1 (.in(bit_1_p4));
  LED led_2 (.in(bit_2_p4));
  xor xor_1 (xor_1_out, sub_borrow_out, BORROW_in_out_p4);
  _1_bit_Subtractor sub (
    .n1(bit_1_p4), .n2(bit_2_p4), .borrow_in(BORROW_in_out_p4), .borrow_out(sub_borrow_out), .res(sub_res));
  // D_FlipFlop BORROW_in_out: pin names not known; wires that end beside it: and_1_out, enable_store, clock, BORROW_in_out_p4
  LED borrow_out (.in(sub_borrow_out));
  and and_2 (and_2_out, clock_4, xor_1_out);
  LED result (.in(sub_res));
  LED borrow_in (.in(BORROW_in_out_p4));
  LED Overflow (.in(and_2_out));
  // D_FlipFlop mem_1: pin names not known; wires that end beside it: sub_res, enable, clock, mem_1_p4
  LED led_3 (.in(mem_1_p4));
  // D_FlipFlop mem_2: pin names not known; wires that end beside it: mem_1_p4, enable, clock, mem_2_p4
  LED led_4 (.in(mem_2_p4));
  // D_FlipFlop mem_3: pin names not known; wires that end beside it: mem_2_p4, enable, clock, mem_3_p4
  LED led_5 (.in(mem_3_p4));

  // Notes on the sheet:
  //   enable: default 1
  //   enable_store: default 1
endmodule
