// Digital circuit main.dig as structural Verilog
module main (
  input  addr1,
  input  addr2,
  input  addr3,
  input  addr1_3,
  input  addr2_3,
  input  addr3_3,
  input  n21,
  input  n22,
  input  n23,
  input  n11,
  input  n12,
  input  n13,
  input  addr1_5,
  input  addr2_5,
  input  addr3_5,
  input  n21_2,
  input  n22_2,
  input  n23_2,
  input  n1i,
  input  n2i,
  input  carry_in,
  input  n2,
  input  n2_2,
  input  n2_3,
  input  n1,
  input  n1_2,
  input  n1_3,
  input  carry_in_2,
  input  val1_4,
  input  val2_4,
  input  val3_4,
  input  \null ,
  input  null_2,
  output val2,
  output val1,
  output addr1_2,
  output val3,
  output addr3_2,
  output addr2_2,
  output val2_2,
  output val1_2,
  output addr1_4,
  output val3_2,
  output addr3_4,
  output addr2_4,
  output val2_3,
  output val1_3,
  output addr1_6,
  output val3_3,
  output addr3_6,
  output addr2_6,
  output carry_out,
  output res,
  output carry_out_2
);

  wire nand_1_out, nand_2_out, nand_3_out, nand_4_out, nand_5_out, nand_6_out, nand_7_out, nand_8_out,
       nand_9_out, nand_10_out, nand_11_out, nand_12_out, nand_13_out, nand_14_out, nand_15_out, nand_16_out,
       nand_17_out, nand_18_out, nand_19_out, nand_20_out, nand_21_out, nand_22_out, nand_23_out,
       nand_24_out, nand_25_out, nand_26_out, nand_27_out, nand_28_out, nand_29_out, nand_30_out,
       nand_31_out, nand_32_out, nand_33_out, nand_34_out, nand_35_out, nand_36_out, nand_37_out,
       nand_38_out, nand_39_out, nand_40_out, nand_41_out, nand_42_out, nand_43_out, nand_44_out,
       nand_45_out, nand_46_out, nand_47_out, nand_48_out, nand_49_out, nand_50_out, nand_51_out,
       nand_52_out, nand_53_out, nand_54_out, nand_55_out, nand_56_out, nand_57_out, nand_58_out,
       nand_59_out, nand_60_out, nand_61_out, nand_62_out, nand_63_out, nand_64_out, nand_65_out,
       nand_66_out, nand_67_out, nand_68_out, nand_69_out, nand_70_out, nand_71_out, nand_72_out,
       nand_73_out, nand_74_out, nand_75_out, nand_76_out, nand_77_out, nand_78_out, nand_79_out,
       nand_80_out, nand_81_out, nand_82_out, nand_83_out, nand_84_out, nand_85_out, nand_86_out,
       nand_87_out, nand_88_out, nand_89_out, nand_90_out, nand_91_out, nand_92_out, nand_93_out,
       nand_94_out, nand_95_out, nand_96_out, nand_97_out, nand_98_out, nand_99_out, nand_100_out,
       nand_101_out, nand_102_out, nand_103_out, nand_104_out, nand_105_out, nand_106_out, nand_107_out,
       nand_108_out, nand_109_out, nand_110_out, nand_111_out, nand_112_out, nand_113_out, nand_114_out,
       nand_115_out, nand_116_out, nand_117_out, nand_118_out, nand_119_out, nand_120_out, nand_121_out,
       nand_122_out, nand_123_out, nand_124_out, nand_125_out, nand_126_out, nand_127_out, nand_128_out,
       nand_129_out, nand_130_out, nand_131_out, nand_132_out, nand_133_out, nand_134_out, nand_135_out,
       nand_136_out, nand_137_out, nand_138_out, nand_139_out, nand_140_out, nand_141_out, nand_142_out,
       nand_143_out, nand_144_out, nand_145_out, nand_146_out, nand_147_out, nand_149_out, nand_150_out,
       nand_151_out, nand_152_out, nand_153_out, nand_154_out, nand_155_out, nand_156_out, nand_157_out,
       nand_158_out, nand_159_out, nand_160_out, nand_161_out, nand_162_out, nand_163_out, nand_164_out,
       nand_165_out, nand_166_out, nand_167_out, nand_168_out, nand_169_out, nand_170_out, nand_171_out,
       nand_172_out, nand_173_out, nand_174_out, nand_175_out, nand_176_out, nand_177_out, nand_178_out,
       nand_179_out, nand_180_out, nand_181_out, nand_182_out, nand_183_out, nand_184_out, nand_185_out,
       nand_186_out, nand_187_out, nand_188_out, nand_189_out, nand_190_out, nand_191_out, nand_192_out,
       nand_193_out, nand_194_out, nand_195_out, nand_196_out, nand_197_out, nand_198_out, nand_199_out,
       nand_200_out, nand_201_out, nand_202_out, nand_203_out, nand_204_out, nand_205_out, nand_206_out,
       nand_207_out, nand_208_out, nand_209_out, nand_210_out, nand_211_out, nand_212_out, nand_213_out,
       nand_214_out, nand_215_out, nand_216_out, nand_217_out, nand_218_out, nand_219_out, nand_220_out,
       nand_221_out, nand_222_out, nand_223_out, nand_224_out, nand_225_out, nand_226_out, nand_227_out,
       nand_228_out, nand_229_out, nand_230_out, nand_231_out, nand_232_out, nand_233_out, nand_234_out,
       nand_235_out, nand_236_out, nand_237_out, nand_238_out, nand_239_out, nand_240_out, nand_241_out,
       nand_242_out, nand_243_out, nand_246_out, nand_247_out, nand_248_out, nand_249_out, nand_250_out,
       nand_251_out, nand_252_out, nand_253_out, nand_254_out, nand_255_out, nand_256_out, nand_257_out,
       nand_258_out, nand_259_out, nand_260_out, nand_264_out, nand_265_out, nand_266_out, nand_267_out,
       nand_268_out, nand_269_out, nand_270_out;

  _7_segment _7_segment_1 ();  // open: top_1, top_2, top_3, top_4, bot_1, bot_2, bot_3, bot_4
  nand nand_1 (nand_1_out, val1_4, val1_4);
  nand nand_2 (nand_2_out, val3_4, val3_4);
  nand nand_3 (nand_3_out, val2_4, val2_4);
  nand nand_4 (nand_4_out, val1_4, val1_4);
  nand nand_5 (nand_5_out, val3_4, val3_4);
  nand nand_6 (nand_6_out, val3_4, val3_4);
  nand nand_7 (nand_7_out, val2_4, val2_4);
  nand nand_8 (nand_8_out, val3_4, val3_4);
  nand nand_9 (nand_9_out, val2_4, val2_4);
  nand nand_10 (nand_10_out, val3_4, val3_4);
  nand nand_11 (nand_11_out, val1_4, nand_9_out);
  nand nand_12 (nand_12_out, nand_1_out, val2_4);
  nand nand_13 (nand_13_out, val2_4, nand_10_out);
  nand nand_14 (nand_14_out, val2_4, nand_2_out);
  nand nand_15 (nand_15_out, val1_4, nand_3_out);
  nand nand_16 (nand_16_out, nand_4_out, nand_5_out);
  nand nand_17 (nand_17_out, val2_4, nand_6_out);
  nand nand_18 (nand_18_out, nand_7_out, nand_8_out);
  nand nand_19 (nand_19_out, nand_17_out, nand_17_out);
  nand nand_20 (nand_20_out, nand_18_out, nand_18_out);
  nand nand_21 (nand_21_out, nand_11_out, nand_11_out);
  nand nand_22 (nand_22_out, nand_12_out, nand_12_out);
  nand nand_23 (nand_23_out, nand_13_out, nand_13_out);
  nand nand_24 (nand_24_out, nand_14_out, nand_14_out);
  nand nand_25 (nand_25_out, nand_15_out, nand_15_out);
  nand nand_26 (nand_26_out, nand_16_out, nand_16_out);
  nand nand_27 (nand_27_out, val1_4, val1_4);
  nand nand_28 (nand_28_out, val3_4, val3_4);
  nand nand_29 (nand_29_out, val1_4, val1_4);
  nand nand_30 (nand_30_out, val3_4, val3_4);
  nand nand_31 (nand_31_out, val2_4, val2_4);
  nand nand_32 (nand_32_out, val1_4, val1_4);
  nand nand_33 (nand_33_out, val3_4, val3_4);
  nand nand_34 (nand_34_out, val2_4, val2_4);
  nand nand_35 (nand_35_out, val1_4, val1_4);
  nand nand_36 (nand_36_out, val3_4, val3_4);
  nand nand_37 (nand_37_out, nand_22_out, nand_22_out);
  nand nand_38 (nand_38_out, nand_23_out, nand_23_out);
  nand nand_39 (nand_39_out, nand_61_out, nand_61_out);
  nand nand_40 (nand_40_out, nand_25_out, nand_25_out);
  nand nand_41 (nand_41_out, nand_27_out, nand_28_out);
  nand nand_42 (nand_42_out, nand_29_out, val2_4);
  nand nand_43 (nand_43_out, val2_4, nand_30_out);
  nand nand_44 (nand_44_out, val1_4, nand_31_out);
  nand nand_45 (nand_45_out, nand_32_out, nand_33_out);
  nand nand_46 (nand_46_out, nand_45_out, nand_45_out);
  nand nand_47 (nand_47_out, nand_34_out, nand_34_out);
  nand nand_48 (nand_48_out, nand_35_out, nand_35_out);
  nand nand_49 (nand_49_out, nand_36_out, nand_36_out);
  nand nand_50 (nand_50_out, val3_4, val3_4);
  nand nand_51 (nand_51_out, val1_4, val1_4);
  nand nand_52 (nand_52_out, nand_26_out, nand_26_out);
  nand nand_53 (nand_53_out, nand_19_out, nand_19_out);
  nand nand_54 (nand_54_out, nand_20_out, nand_20_out);
  nand nand_55 (nand_55_out, nand_21_out, nand_21_out);
  nand nand_56 (nand_56_out, nand_60_out, nand_60_out);
  nand nand_57 (nand_57_out, nand_24_out, nand_24_out);
  nand nand_58 (nand_58_out, val3_4, val1_4);
  nand nand_59 (nand_59_out, nand_54_out, nand_55_out);
  nand nand_60 (nand_60_out, nand_37_out, nand_38_out);
  nand nand_61 (nand_61_out, nand_56_out, nand_57_out);
  nand nand_62 (nand_62_out, nand_39_out, nand_40_out);
  nand nand_63 (nand_63_out, nand_41_out, nand_41_out);
  nand nand_64 (nand_64_out, nand_42_out, nand_42_out);
  nand nand_65 (nand_65_out, nand_43_out, nand_43_out);
  nand nand_66 (nand_66_out, nand_44_out, nand_44_out);
  nand nand_67 (nand_67_out, nand_46_out, nand_47_out);
  nand nand_68 (nand_68_out, nand_48_out, nand_49_out);
  nand nand_69 (nand_69_out, nand_68_out, nand_68_out);
  nand nand_70 (nand_70_out, val2_4, val2_4);
  nand nand_71 (nand_71_out, nand_50_out, nand_51_out);
  nand nand_72 (nand_72_out, nand_58_out, nand_58_out);
  nand nand_73 (nand_73_out, nand_52_out, nand_53_out);
  nand nand_74 (nand_74_out, nand_72_out, nand_72_out);
  nand nand_75 (nand_75_out, val2_4, val2_4);
  nand nand_76 (nand_76_out, nand_69_out, nand_70_out);
  nand nand_77 (nand_77_out, nand_71_out, nand_71_out);
  nand nand_78 (nand_78_out, nand_63_out, nand_63_out);
  nand nand_79 (nand_79_out, nand_64_out, nand_64_out);
  nand nand_80 (nand_80_out, nand_85_out, nand_85_out);
  nand nand_81 (nand_81_out, nand_65_out, nand_65_out);
  nand nand_82 (nand_82_out, nand_86_out, nand_86_out);
  nand nand_83 (nand_83_out, nand_66_out, nand_66_out);
  nand nand_84 (nand_84_out, nand_74_out, nand_75_out);
  nand nand_85 (nand_85_out, nand_78_out, nand_79_out);
  nand nand_86 (nand_86_out, nand_80_out, nand_81_out);
  nand nand_87 (nand_87_out, nand_82_out, nand_83_out);
  nand nand_88 (nand_88_out, nand_77_out, nand_77_out);
  nand nand_89 (nand_89_out, nand_84_out, nand_84_out);
  nand nand_90 (nand_90_out, nand_88_out, nand_89_out);
  Seven_Seg seven_seg_1 (
    .a(nand_90_out), .b(nand_76_out), .c(nand_67_out), .d(nand_87_out), .e(nand_73_out), .f(nand_59_out),
    .g(nand_62_out), .dp(\null ));
  nand nand_91 (nand_91_out, n1_3, n2_3);
  nand nand_92 (nand_92_out, n1, n2);
  nand nand_93 (nand_93_out, n1_2, n2_2);
  nand nand_94 (nand_94_out, n1_3, nand_91_out);
  nand nand_95 (nand_95_out, nand_91_out, n2_3);
  nand nand_96 (nand_96_out, n1, nand_92_out);
  nand nand_97 (nand_97_out, nand_92_out, n2);
  nand nand_98 (nand_98_out, n1_2, nand_93_out);
  nand nand_99 (nand_99_out, nand_93_out, n2_2);
  nand nand_100 (nand_100_out, n1_2, n2_2);
  nand nand_101 (nand_101_out, n1_2, nand_150_out);
  nand nand_102 (nand_102_out, n2_2, nand_150_out);
  nand nand_103 (nand_103_out, n1_3, n2_3);
  nand nand_104 (nand_104_out, n1_3, carry_in_2);
  nand nand_105 (nand_105_out, n2_3, carry_in_2);
  nand nand_106 (nand_106_out, n1, n2);
  nand nand_107 (nand_107_out, n1, nand_149_out);
  nand nand_108 (nand_108_out, n2, nand_149_out);
  nand nand_109 (nand_109_out, nand_94_out, nand_95_out);
  nand nand_110 (nand_110_out, nand_96_out, nand_97_out);
  nand nand_111 (nand_111_out, nand_98_out, nand_99_out);
  nand nand_112 (nand_112_out, nand_100_out, nand_100_out);
  nand nand_113 (nand_113_out, nand_101_out, nand_101_out);
  nand nand_114 (nand_114_out, nand_102_out, nand_102_out);
  nand nand_115 (nand_115_out, nand_103_out, nand_103_out);
  nand nand_116 (nand_116_out, nand_104_out, nand_104_out);
  nand nand_117 (nand_117_out, nand_105_out, nand_105_out);
  nand nand_118 (nand_118_out, nand_106_out, nand_106_out);
  nand nand_119 (nand_119_out, nand_107_out, nand_107_out);
  nand nand_120 (nand_120_out, nand_108_out, nand_108_out);
  nand nand_121 (nand_121_out, nand_113_out, nand_113_out);
  nand nand_122 (nand_122_out, nand_114_out, nand_114_out);
  nand nand_123 (nand_123_out, nand_116_out, nand_116_out);
  nand nand_124 (nand_124_out, nand_117_out, nand_117_out);
  nand nand_125 (nand_125_out, nand_119_out, nand_119_out);
  nand nand_126 (nand_126_out, nand_120_out, nand_120_out);
  nand nand_127 (nand_127_out, nand_150_out, nand_111_out);
  nand nand_128 (nand_128_out, carry_in_2, nand_109_out);
  nand nand_129 (nand_129_out, nand_149_out, nand_110_out);
  nand nand_130 (nand_130_out, nand_121_out, nand_122_out);
  nand nand_131 (nand_131_out, nand_123_out, nand_124_out);
  nand nand_132 (nand_132_out, nand_125_out, nand_126_out);
  nand nand_133 (nand_133_out, nand_150_out, nand_127_out);
  nand nand_134 (nand_134_out, nand_127_out, nand_111_out);
  nand nand_135 (nand_135_out, carry_in_2, nand_128_out);
  nand nand_136 (nand_136_out, nand_128_out, nand_109_out);
  nand nand_137 (nand_137_out, nand_149_out, nand_129_out);
  nand nand_138 (nand_138_out, nand_129_out, nand_110_out);
  nand nand_139 (nand_139_out, nand_112_out, nand_112_out);
  nand nand_140 (nand_140_out, nand_130_out, nand_130_out);
  nand nand_141 (nand_141_out, nand_115_out, nand_115_out);
  nand nand_142 (nand_142_out, nand_131_out, nand_131_out);
  nand nand_143 (nand_143_out, nand_118_out, nand_118_out);
  nand nand_144 (nand_144_out, nand_132_out, nand_132_out);
  nand nand_145 (nand_145_out, nand_133_out, nand_134_out);
  nand nand_146 (nand_146_out, nand_135_out, nand_136_out);
  nand nand_147 (nand_147_out, nand_137_out, nand_138_out);
  nand nand_148 (carry_out_2, nand_143_out, nand_144_out);
  nand nand_149 (nand_149_out, nand_139_out, nand_140_out);
  nand nand_150 (nand_150_out, nand_141_out, nand_142_out);
  nand nand_151 (nand_151_out, n1i, n2i);
  nand nand_152 (nand_152_out, nand_147_out, nand_147_out);
  nand nand_153 (nand_153_out, nand_146_out, nand_146_out);
  nand nand_154 (nand_154_out, nand_146_out, nand_146_out);
  nand nand_155 (nand_155_out, nand_145_out, nand_145_out);
  nand nand_156 (nand_156_out, nand_146_out, nand_146_out);
  nand nand_157 (nand_157_out, nand_145_out, nand_145_out);
  nand nand_158 (nand_158_out, nand_147_out, nand_147_out);
  nand nand_159 (nand_159_out, nand_146_out, nand_146_out);
  nand nand_160 (nand_160_out, nand_146_out, nand_146_out);
  nand nand_161 (nand_161_out, nand_145_out, nand_145_out);
  nand nand_162 (nand_162_out, n1i, nand_151_out);
  nand nand_163 (nand_163_out, nand_151_out, n2i);
  nand nand_164 (nand_164_out, nand_158_out, nand_145_out);
  nand nand_165 (nand_165_out, nand_145_out, nand_159_out);
  nand nand_166 (nand_166_out, nand_145_out, nand_160_out);
  nand nand_167 (nand_167_out, nand_147_out, nand_161_out);
  nand nand_168 (nand_168_out, n1i, n2i);
  nand nand_169 (nand_169_out, n1i, carry_in);
  nand nand_170 (nand_170_out, n2i, carry_in);
  nand nand_171 (nand_171_out, nand_152_out, nand_153_out);
  nand nand_172 (nand_172_out, nand_145_out, nand_154_out);
  nand nand_173 (nand_173_out, nand_155_out, nand_156_out);
  nand nand_174 (nand_174_out, nand_147_out, nand_157_out);
  nand nand_175 (nand_175_out, nand_162_out, nand_163_out);
  nand nand_176 (nand_176_out, nand_174_out, nand_174_out);
  nand nand_177 (nand_177_out, nand_164_out, nand_164_out);
  nand nand_178 (nand_178_out, nand_165_out, nand_165_out);
  nand nand_179 (nand_179_out, nand_166_out, nand_166_out);
  nand nand_180 (nand_180_out, nand_167_out, nand_167_out);
  nand nand_181 (nand_181_out, nand_168_out, nand_168_out);
  nand nand_182 (nand_182_out, nand_169_out, nand_169_out);
  nand nand_183 (nand_183_out, nand_170_out, nand_170_out);
  nand nand_184 (nand_184_out, nand_171_out, nand_171_out);
  nand nand_185 (nand_185_out, nand_172_out, nand_172_out);
  nand nand_186 (nand_186_out, nand_173_out, nand_173_out);
  nand nand_187 (nand_187_out, nand_147_out, nand_147_out);
  nand nand_188 (nand_188_out, nand_146_out, nand_146_out);
  nand nand_189 (nand_189_out, nand_147_out, nand_147_out);
  nand nand_190 (nand_190_out, nand_146_out, nand_146_out);
  nand nand_191 (nand_191_out, nand_145_out, nand_145_out);
  nand nand_192 (nand_192_out, nand_147_out, nand_147_out);
  nand nand_193 (nand_193_out, nand_146_out, nand_146_out);
  nand nand_194 (nand_194_out, nand_145_out, nand_145_out);
  nand nand_195 (nand_195_out, nand_147_out, nand_147_out);
  nand nand_196 (nand_196_out, nand_146_out, nand_146_out);
  nand nand_197 (nand_197_out, nand_182_out, nand_182_out);
  nand nand_198 (nand_198_out, nand_183_out, nand_183_out);
  nand nand_199 (nand_199_out, carry_in, nand_175_out);
  nand nand_200 (nand_200_out, nand_187_out, nand_188_out);
  nand nand_201 (nand_201_out, nand_189_out, nand_145_out);
  nand nand_202 (nand_202_out, nand_145_out, nand_190_out);
  nand nand_203 (nand_203_out, nand_147_out, nand_191_out);
  nand nand_204 (nand_204_out, nand_192_out, nand_193_out);
  nand nand_205 (nand_205_out, nand_204_out, nand_204_out);
  nand nand_206 (nand_206_out, nand_194_out, nand_194_out);
  nand nand_207 (nand_207_out, nand_195_out, nand_195_out);
  nand nand_208 (nand_208_out, nand_196_out, nand_196_out);
  nand nand_209 (nand_209_out, nand_146_out, nand_146_out);
  nand nand_210 (nand_210_out, nand_184_out, nand_184_out);
  nand nand_211 (nand_211_out, nand_185_out, nand_185_out);
  nand nand_212 (nand_212_out, nand_186_out, nand_186_out);
  nand nand_213 (nand_213_out, nand_176_out, nand_176_out);
  nand nand_214 (nand_214_out, nand_177_out, nand_177_out);
  nand nand_215 (nand_215_out, nand_178_out, nand_178_out);
  nand nand_216 (nand_216_out, nand_223_out, nand_223_out);
  nand nand_217 (nand_217_out, nand_179_out, nand_179_out);
  nand nand_218 (nand_218_out, nand_238_out, nand_238_out);
  nand nand_219 (nand_219_out, nand_180_out, nand_180_out);
  nand nand_220 (nand_220_out, nand_197_out, nand_198_out);
  nand nand_221 (nand_221_out, nand_147_out, nand_147_out);
  nand nand_222 (nand_222_out, nand_146_out, nand_147_out);
  nand nand_223 (nand_223_out, nand_214_out, nand_215_out);
  nand nand_224 (nand_224_out, nand_218_out, nand_219_out);
  nand nand_225 (nand_225_out, carry_in, nand_199_out);
  nand nand_226 (nand_226_out, nand_199_out, nand_175_out);
  nand nand_227 (nand_227_out, nand_200_out, nand_200_out);
  nand nand_228 (nand_228_out, nand_201_out, nand_201_out);
  nand nand_229 (nand_229_out, nand_202_out, nand_202_out);
  nand nand_230 (nand_230_out, nand_203_out, nand_203_out);
  nand nand_231 (nand_231_out, nand_205_out, nand_206_out);
  nand nand_232 (nand_232_out, nand_207_out, nand_208_out);
  nand nand_233 (nand_233_out, nand_232_out, nand_232_out);
  nand nand_234 (nand_234_out, nand_145_out, nand_145_out);
  nand nand_235 (nand_235_out, nand_209_out, nand_221_out);
  nand nand_236 (nand_236_out, nand_210_out, nand_211_out);
  nand nand_237 (nand_237_out, nand_212_out, nand_213_out);
  nand nand_238 (nand_238_out, nand_216_out, nand_217_out);
  nand nand_239 (nand_239_out, nand_181_out, nand_181_out);
  nand nand_240 (nand_240_out, nand_220_out, nand_220_out);
  nand nand_241 (nand_241_out, nand_222_out, nand_222_out);
  nand nand_242 (nand_242_out, nand_241_out, nand_241_out);
  nand nand_243 (nand_243_out, nand_145_out, nand_145_out);
  nand nand_244 (res, nand_225_out, nand_226_out);
  nand nand_245 (carry_out, nand_239_out, nand_240_out);
  nand nand_246 (nand_246_out, nand_233_out, nand_234_out);
  nand nand_247 (nand_247_out, nand_235_out, nand_235_out);
  nand nand_248 (nand_248_out, nand_227_out, nand_227_out);
  nand nand_249 (nand_249_out, nand_228_out, nand_228_out);
  nand nand_250 (nand_250_out, nand_256_out, nand_256_out);
  nand nand_251 (nand_251_out, nand_230_out, nand_230_out);
  nand nand_252 (nand_252_out, nand_242_out, nand_243_out);
  nand nand_253 (nand_253_out, nand_255_out, nand_255_out);
  nand nand_254 (nand_254_out, nand_229_out, nand_229_out);
  nand nand_255 (nand_255_out, nand_248_out, nand_249_out);
  nand nand_256 (nand_256_out, nand_253_out, nand_254_out);
  nand nand_257 (nand_257_out, nand_250_out, nand_251_out);
  nand nand_258 (nand_258_out, nand_247_out, nand_247_out);
  nand nand_259 (nand_259_out, nand_252_out, nand_252_out);
  Seven_Seg seven_seg_2 (
    .a(nand_260_out), .b(nand_246_out), .c(nand_231_out), .d(nand_257_out), .e(nand_236_out),
    .f(nand_237_out), .g(nand_224_out), .dp(null_2));
  nand nand_260 (nand_260_out, nand_258_out, nand_259_out);
  nand nand_261 (val1_3, n21_2, n21_2);
  nand nand_262 (val2_3, n22_2, n22_2);
  nand nand_263 (val3_3, n23_2, n23_2);
  nand nand_264 (nand_264_out, n11, n11);
  nand nand_265 (nand_265_out, n21, n21);
  nand nand_266 (nand_266_out, n12, n12);
  nand nand_267 (nand_267_out, n22, n22);
  nand nand_268 (nand_268_out, n13, n13);
  nand nand_269 (nand_269_out, n23, n23);
  nand nand_270 (nand_270_out, addr1, addr1);
  nand nand_271 (val1_2, nand_264_out, nand_265_out);
  nand nand_272 (val2_2, nand_266_out, nand_267_out);
  nand nand_273 (val3_2, nand_268_out, nand_269_out);
  nand nand_274 (val1, nand_270_out, addr1);

  assign addr1_2 = addr1;
  assign addr1_4 = addr1_3;
  assign addr1_6 = addr1_5;
  assign addr2_2 = addr2;
  assign addr2_4 = addr2_3;
  assign addr2_6 = addr2_5;
  assign addr3_2 = addr3;
  assign addr3_4 = addr3_3;
  assign addr3_6 = addr3_5;
  assign val2 = val1;
  assign val3 = val1;

  // Notes on the sheet:
  //   val_3
  //   val_2
  //   val_1
  //   7 SEGMENT CI DISPLAY
  //   I_7
  //   I_3
  //   I_5
  //   I_6
  //   I_2
  //   I_4
  //   I_1
  //   n_1 bit
  //   n_2 bit
  //   carry_in bit
  //   n1i+n2i
  //   n1i+carry_in
  //   n2i+carry_in
  //   3 BIT ADDER
  //   res bit
  //   carry_out bit
  //   1 BIT ADDER
  //   INV CI
  //   OR CI
  //   INIT CI
endmodule
